# Fritzing sketch 光センサ (saved by Fritzing 0.8.7b)
breadboards: 1

parts:
  aruduino = Arduino Uno (Rev3)
  R1 = Photocell (LDR) [package=THT]
  R2 = Resistor [tolerance=±5% resistance=10k package=THT]

nets:
  N1: aruduino.A0, R1.pin_0, R2.Pin_1
  N2: aruduino.5V, R1.pin_1
  N3: aruduino.GND, R2.Pin_0
