# Fritzing sketch infrared_proximity (saved by Fritzing 0.9.2b)
breadboards: 1

parts:
  part = Arduino Uno (Rev3)
  part_2 = Infrared Proximity Sensor

nets:
  N1: part.A0, part_2.Vout
  GND: part.GND, part_2.GND
  5V: part.5V, part_2.Vcc
